# Fritzing sketch knock_diagram (saved by Fritzing 0.7.10b)
breadboards: 1

parts:
  Arduino1 = Arduino
  LED1 = LED - 5mm [color="Red (633nm)" package="5 mm [THT]"]
  LED2 = LED - 5mm [color="Green (570nm)" package="5 mm [THT]"]
  J1 = Piezo Speaker
  R1 = Resistor [tolerance=±5% resistance=4.7k package=THT]
  J2 = Basic Servo
  S1 = Pushbutton [package="[THT]"]
  R2 = Resistor [tolerance=±5% resistance=10k package=THT]
  J3 = Piezo Speaker

nets:
  GND: Arduino1.GND, LED1.anode, LED2.anode, J1.pin1, R1.Pin_1, J2.gnd, R2.Pin_1, J3.pin1
  N1: Arduino1.D13, LED1.cathode
  N2: Arduino1.D12, J2.pulse
  N3: Arduino1.D11, LED2.cathode
  N4: Arduino1.D9, J3.pin2
  N5: Arduino1.D2, S1.Pin_1, S1.Pin_2, R2.Pin_0
  +5V: Arduino1.+5V, J2.vcc, S1.Pin_3, S1.Pin_4
  N6: Arduino1.A0, J1.pin2, R1.Pin_0
